// Logisim project R TYpe datapath.circ as structural Verilog: 20 circuits, main circuit NOT IC
module main (
  input  [15:0] WRITE_DATA,
  input  Write_enabler,
  input  [3:0] RS_SELECTOR,
  input  [3:0] RD,
  input  [3:0] RT_SELECTOR,
  input  Clock,
  input  Register_clear,
  output [15:0] Data1_RS,
  output [15:0] Data2_RT
);

  wire and_1_out, and_2_out, and_3_out, and_4_out, and_5_out, and_6_out, and_7_out, and_8_out, and_9_out,
       and_10_out, and_11_out, and_12_out, and_13_out, and_14_out, and_15_out, and_16_out, decoder_1_out0,
       decoder_1_out1, decoder_1_out2, decoder_1_out3, decoder_1_out4, decoder_1_out5, decoder_1_out6,
       decoder_1_out7, decoder_1_out8, decoder_1_out9, decoder_1_out10, decoder_1_out11, decoder_1_out12,
       decoder_1_out13, decoder_1_out14, decoder_1_out15;
  wire [15:0] s0_q, s1_q, s2_q, s3_q, s4_q, s5_q, s6_q, s7_q, s8_q, s9_q, s10_q, s11_q, s12_q, s13_q, s14_q,
       s15_q;

  Decoder #(.select(4), .enable("false")) decoder_1 (
    .out0(decoder_1_out0), .out1(decoder_1_out1), .out2(decoder_1_out2), .out3(decoder_1_out3),
    .out4(decoder_1_out4), .out5(decoder_1_out5), .out6(decoder_1_out6), .out7(decoder_1_out7),
    .out8(decoder_1_out8), .out9(decoder_1_out9), .out10(decoder_1_out10), .out11(decoder_1_out11),
    .out12(decoder_1_out12), .out13(decoder_1_out13), .out14(decoder_1_out14), .out15(decoder_1_out15),
    .sel(RD));
  and and_1 (and_1_out, Write_enabler, decoder_1_out0);
  and and_2 (and_2_out, Write_enabler, decoder_1_out1);
  and and_3 (and_3_out, Write_enabler, decoder_1_out2);
  and and_4 (and_4_out, Write_enabler, decoder_1_out3);
  and and_5 (and_5_out, Write_enabler, decoder_1_out4);
  and and_6 (and_6_out, Write_enabler, decoder_1_out5);
  and and_7 (and_7_out, Write_enabler, decoder_1_out6);
  and and_8 (and_8_out, Write_enabler, decoder_1_out7);
  and and_9 (and_9_out, Write_enabler, decoder_1_out8);
  and and_10 (and_10_out, Write_enabler, decoder_1_out9);
  and and_11 (and_11_out, Write_enabler, decoder_1_out10);
  and and_12 (and_12_out, Write_enabler, decoder_1_out11);
  and and_13 (and_13_out, Write_enabler, decoder_1_out12);
  and and_14 (and_14_out, Write_enabler, decoder_1_out13);
  and and_15 (and_15_out, Write_enabler, decoder_1_out14);
  and and_16 (and_16_out, Write_enabler, decoder_1_out15);
  Register #(.width(16)) s0 (.D(WRITE_DATA), .en(and_1_out), .Q(s0_q), .clk(Clock), .clr(Register_clear));
  Register #(.width(16)) s1 (.D(WRITE_DATA), .en(and_2_out), .Q(s1_q), .clk(Clock), .clr(Register_clear));
  Register #(.width(16)) s2 (.D(WRITE_DATA), .en(and_3_out), .Q(s2_q), .clk(Clock), .clr(Register_clear));
  Register #(.width(16)) s3 (.D(WRITE_DATA), .en(and_4_out), .Q(s3_q), .clk(Clock), .clr(Register_clear));
  Register #(.width(16)) s4 (.D(WRITE_DATA), .en(and_5_out), .Q(s4_q), .clk(Clock), .clr(Register_clear));
  Register #(.width(16)) s5 (.D(WRITE_DATA), .en(and_6_out), .Q(s5_q), .clk(Clock), .clr(Register_clear));
  Register #(.width(16)) s6 (.D(WRITE_DATA), .en(and_7_out), .Q(s6_q), .clk(Clock), .clr(Register_clear));
  Register #(.width(16)) s7 (.D(WRITE_DATA), .en(and_8_out), .Q(s7_q), .clk(Clock), .clr(Register_clear));
  Register #(.width(16)) s8 (.D(WRITE_DATA), .en(and_9_out), .Q(s8_q), .clk(Clock), .clr(Register_clear));
  Register #(.width(16)) s9 (.D(WRITE_DATA), .en(and_10_out), .Q(s9_q), .clk(Clock), .clr(Register_clear));
  Register #(.width(16)) s10 (.D(WRITE_DATA), .en(and_11_out), .Q(s10_q), .clk(Clock), .clr(Register_clear));
  Register #(.width(16)) s11 (.D(WRITE_DATA), .en(and_12_out), .Q(s11_q), .clk(Clock), .clr(Register_clear));
  Register #(.width(16)) s12 (.D(WRITE_DATA), .en(and_13_out), .Q(s12_q), .clk(Clock), .clr(Register_clear));
  Register #(.width(16)) s13 (.D(WRITE_DATA), .en(and_14_out), .Q(s13_q), .clk(Clock), .clr(Register_clear));
  Register #(.width(16)) s14 (.D(WRITE_DATA), .en(and_15_out), .Q(s14_q), .clk(Clock), .clr(Register_clear));
  Register #(.width(16)) s15 (.D(WRITE_DATA), .en(and_16_out), .Q(s15_q), .clk(Clock), .clr(Register_clear));
  Multiplexer #(.select(4), .width(16), .enable("false")) multiplexer_1 (
    .in0(s0_q), .in1(s1_q), .in2(s2_q), .in3(s3_q), .in4(s4_q), .in5(s5_q), .in6(s6_q), .in7(s7_q),
    .in8(s8_q), .in9(s9_q), .in10(s10_q), .in11(s11_q), .in12(s12_q), .in13(s13_q), .in14(s14_q),
    .in15(s15_q), .out(Data1_RS), .sel(RS_SELECTOR));
  Multiplexer #(.select(4), .width(16), .enable("false")) multiplexer_2 (
    .in0(s0_q), .in1(s1_q), .in2(s3_q), .in3(s4_q), .in4(s4_q), .in5(s5_q), .in6(s6_q), .in7(s7_q),
    .in8(s8_q), .in9(s9_q), .in10(s10_q), .in11(s11_q), .in12(s12_q), .in13(s13_q), .in14(s14_q),
    .in15(s15_q), .out(Data2_RT), .sel(RT_SELECTOR));
endmodule

module NOT_IC (
  input  in_1,
  input  in_2,
  input  in_3,
  input  in_4,
  input  in_5,
  input  in_6,
  output out_7,
  output out_8,
  output out_9,
  output out_10,
  output out_11,
  output out_12
);

  not not_1 (out_7, in_1);
  not not_2 (out_8, in_2);
  not not_3 (out_9, in_3);
  not not_4 (out_10, in_4);
  not not_5 (out_11, in_5);
  not not_6 (out_12, in_6);
endmodule

module AND_IC (
  input  in_1,
  input  in_2,
  input  in_3,
  input  in_4,
  input  in_5,
  input  in_6,
  input  in_7,
  input  in_8,
  output out_9,
  output out_10,
  output out_11,
  output out_12
);

  and and_1 (out_9, in_1, in_2);
  and and_2 (out_10, in_3, in_4);
  and and_3 (out_11, in_5, in_6);
  and and_4 (out_12, in_7, in_8);
endmodule

module OR_IC (
  input  in_1,
  input  in_2,
  input  in_3,
  input  in_4,
  input  in_5,
  input  in_6,
  input  in_7,
  input  in_8,
  output out_9,
  output out_10,
  output out_11,
  output out_12
);

  or or_1 (out_9, in_1, in_2);
  or or_2 (out_10, in_3, in_4);
  or or_3 (out_11, in_5, in_6);
  or or_4 (out_12, in_7, in_8);
endmodule

module NOR_IC (
  input  in_1,
  input  in_2,
  input  in_3,
  input  in_4,
  input  in_5,
  input  in_6,
  input  in_7,
  input  in_8,
  output out_9,
  output out_10,
  output out_11,
  output out_12
);

  nor nor_1 (out_9, in_1, in_2);
  nor nor_2 (out_10, in_3, in_4);
  nor nor_3 (out_11, in_5, in_6);
  nor nor_4 (out_12, in_7, in_8);
endmodule

module NAND_IC (
  input  in_1,
  input  in_2,
  input  in_3,
  input  in_4,
  input  in_5,
  input  in_6,
  input  in_7,
  input  in_8,
  output out_9,
  output out_10,
  output out_11,
  output out_12
);

  nand nand_1 (out_9, in_1, in_2);
  nand nand_2 (out_10, in_3, in_4);
  nand nand_3 (out_11, in_5, in_6);
  nand nand_4 (out_12, in_7, in_8);
endmodule

module XOR_IC (
  input  in_1,
  input  in_2,
  input  in_3,
  input  in_4,
  input  in_5,
  input  in_6,
  input  in_7,
  input  in_8,
  output out_9,
  output out_10,
  output out_11,
  output out_12
);

  xor xor_1 (out_9, in_1, in_2);
  xor xor_2 (out_10, in_3, in_4);
  xor xor_3 (out_11, in_5, in_6);
  xor xor_4 (out_12, in_7, in_8);
endmodule

module _4_1_MUX (
  input  _1,
  input  _2,
  input  _3,
  input  _4,
  input  S2,
  input  S1,
  output out_7
);

  wire and_1_out, and_2_out, and_3_out, and_4_out, not_1_out, not_2_out;

  not not_1 (not_1_out, S2);
  not not_2 (not_2_out, S1);
  and and_1 (and_1_out, _1, not_2_out, not_1_out);
  and and_2 (and_2_out, _2, S1, not_1_out);
  and and_3 (and_3_out, _3, not_2_out, S2);
  and and_4 (and_4_out, _4, S1, S2);
  or or_1 (out_7, and_1_out, and_2_out, and_3_out, and_4_out);
endmodule

module D_Flip_flop_IC (
  input  Pre_set,
  input  Clock,
  input  D,
  input  Clear,
  output out_5,
  output out_6
);

  wire nand_1_out, nand_2_out, nand_3_out, nand_4_out, not_1_out, not_2_out;

  not not_1 (not_1_out, Pre_set);
  not not_2 (not_2_out, Clear);
  nand nand_1 (nand_1_out, not_1_out, nand_4_out, nand_2_out);
  nand nand_2 (nand_2_out, nand_1_out, Clock, not_2_out);
  nand nand_3 (nand_3_out, Clock, nand_4_out, nand_2_out);
  nand nand_4 (nand_4_out, D, nand_3_out, not_2_out);
  nand nand_5 (out_5, not_1_out, nand_2_out, out_6);
  nand nand_6 (out_6, out_5, nand_3_out, not_2_out);
endmodule

module _4_bit_adder_IC (
  input  A1,
  input  B1,
  input  CARRY_ON,
  input  A2,
  input  B2,
  input  A3,
  input  B3,
  input  A4,
  input  B4,
  output SUM1,
  output SUM2,
  output SUM3,
  output SUM4,
  output CARRY_OUT
);

  wire and_1_out, and_2_out, and_3_out, and_4_out, and_5_out, and_6_out, and_7_out, and_8_out, or_1_out,
       or_3_out, or_4_out, xor_1_out, xor_2_out, xor_3_out, xor_4_out;

  and and_1 (and_1_out, A3, B3);
  xor xor_1 (xor_1_out, A4, B4);
  and and_2 (and_2_out, A4, B4);
  and and_3 (and_3_out, A1, B1);
  and and_4 (and_4_out, A2, B2);
  xor xor_2 (xor_2_out, A3, B3);
  and and_5 (and_5_out, xor_1_out, or_1_out);
  xor xor_3 (xor_3_out, A1, B1);
  xor xor_4 (xor_4_out, A2, B2);
  and and_6 (and_6_out, xor_2_out, or_4_out);
  and and_7 (and_7_out, xor_3_out, CARRY_ON);
  and and_8 (and_8_out, xor_4_out, or_3_out);
  xor xor_5 (SUM4, xor_1_out, or_1_out);
  xor xor_6 (SUM3, xor_2_out, or_4_out);
  or or_1 (or_1_out, and_6_out, and_1_out);
  or or_2 (CARRY_OUT, and_5_out, and_2_out);
  xor xor_7 (SUM1, xor_3_out, CARRY_ON);
  or or_3 (or_3_out, and_7_out, and_3_out);
  xor xor_8 (SUM2, xor_4_out, or_3_out);
  or or_4 (or_4_out, and_8_out, and_4_out);
endmodule

module _2_bit_logic_IC (
  input  A1,
  input  B1,
  input  A2,
  input  B2,
  input  S1,
  input  S2,
  output out_7,
  output F2
);

  wire and_ic_1_out_9, and_ic_1_out_10, nor_ic_1_out_9, nor_ic_1_out_10, not_ic_1_out_7, not_ic_1_out_8,
       or_ic_1_out_9, or_ic_1_out_10;

  OR_IC or_ic_1 (
    .in_1(A1), .in_2(B1), .in_3(A2), .in_4(B2), .out_9(or_ic_1_out_9), .out_10(or_ic_1_out_10));  // open: in_5, in_6, in_7, in_8, out_11, out_12
  NOT_IC not_ic_1 (
    .in_1(A1), .in_2(A2), .out_7(not_ic_1_out_7), .out_8(not_ic_1_out_8));  // open: in_3, in_4, in_5, in_6, out_9, out_10, out_11, out_12
  NOR_IC nor_ic_1 (
    .in_1(A1), .in_2(B1), .in_3(A2), .in_4(B2), .out_9(nor_ic_1_out_9), .out_10(nor_ic_1_out_10));  // open: in_5, in_6, in_7, in_8, out_11, out_12
  AND_IC and_ic_1 (
    .in_1(A1), .in_2(B1), .in_3(A2), .in_4(B2), .out_9(and_ic_1_out_9), .out_10(and_ic_1_out_10));  // open: in_5, in_6, in_7, in_8, out_11, out_12
  _4_1_MUX u_4_1_mux_1 (
    ._1(and_ic_1_out_9), ._2(or_ic_1_out_9), ._3(not_ic_1_out_7), ._4(nor_ic_1_out_9), .S2(S2), .S1(S1),
    .out_7(out_7));
  _4_1_MUX u_4_1_mux_2 (
    ._1(and_ic_1_out_10), ._2(or_ic_1_out_10), ._3(not_ic_1_out_8), ._4(nor_ic_1_out_10), .S2(S2), .S1(S1),
    .out_7(F2));
endmodule

module Accessing_the_register_file_using_the_register_file (
  input  [15:0] Write_data,
  input  PC_Clear,
  input  Write_enabler,
  input  Clear_register,
  output [3:0] OP_code,
  output [3:0] RS,
  output [3:0] RT,
  output [3:0] RD,
  output [15:0] Data1_RS,
  output [15:0] Data2_RT
);

  wire Clock_out;
  wire [15:0] adder_1_out, register_1_q;

  Register #(.width(16)) register_1 (.D(adder_1_out), .Q(register_1_q), .clk(Clock_out), .clr(PC_Clear));  // open: en
  Clock Clock (.out(Clock_out));
  Adder #(.width(16)) adder_1 (.a(register_1_q), .b(16'h1), .out(adder_1_out));  // open: cin, cout
  ROM #(.addrWidth(16), .dataWidth(16)) rom_1 (.addr(register_1_q), .data({OP_code, RS, RT, RD}));  // open: sel
  _16_bit_register_file u_16_bit_register_file_1 (
    .Write_enabler(Write_enabler), .RD(RD), .Clock(Clock_out), .Data1_RS(Data1_RS), .RS_SELECTOR(RS),
    .Data2_RT(Data2_RT), .RT_SELECTOR(RT), .Register_clear(Clear_register), .Bin(Write_data));

  // Notes on the sheet:
  //   JOBAER AHMED 
  //   ID- 426 
endmodule

module _16_bit_register_file (
  input  [15:0] Bin,
  input  Write_enabler,
  input  [3:0] RS_SELECTOR,
  input  [3:0] RD,
  input  [3:0] RT_SELECTOR,
  input  Clock,
  input  Register_clear,
  output [15:0] Data1_RS,
  output [15:0] Data2_RT
);

  wire and_1_out, and_2_out, and_3_out, and_4_out, and_5_out, and_6_out, and_7_out, and_8_out, and_9_out,
       and_10_out, and_11_out, and_12_out, and_13_out, and_14_out, and_15_out, and_16_out, decoder_1_out0,
       decoder_1_out1, decoder_1_out2, decoder_1_out3, decoder_1_out4, decoder_1_out5, decoder_1_out6,
       decoder_1_out7, decoder_1_out8, decoder_1_out9, decoder_1_out10, decoder_1_out11, decoder_1_out12,
       decoder_1_out13, decoder_1_out14, decoder_1_out15;
  wire [15:0] s0_q, s1_q, s2_q, s3_q, s4_q, s5_q, s6_q, s7_q, s8_q, s9_q, s10_q, s11_q, s12_q, s13_q, s14_q,
       s15_q;

  Decoder #(.select(4), .enable("false")) decoder_1 (
    .out0(decoder_1_out0), .out1(decoder_1_out1), .out2(decoder_1_out2), .out3(decoder_1_out3),
    .out4(decoder_1_out4), .out5(decoder_1_out5), .out6(decoder_1_out6), .out7(decoder_1_out7),
    .out8(decoder_1_out8), .out9(decoder_1_out9), .out10(decoder_1_out10), .out11(decoder_1_out11),
    .out12(decoder_1_out12), .out13(decoder_1_out13), .out14(decoder_1_out14), .out15(decoder_1_out15),
    .sel(RD));
  and and_1 (and_1_out, Write_enabler, decoder_1_out0);
  and and_2 (and_2_out, Write_enabler, decoder_1_out1);
  and and_3 (and_3_out, Write_enabler, decoder_1_out2);
  and and_4 (and_4_out, Write_enabler, decoder_1_out3);
  and and_5 (and_5_out, Write_enabler, decoder_1_out4);
  and and_6 (and_6_out, Write_enabler, decoder_1_out5);
  and and_7 (and_7_out, Write_enabler, decoder_1_out6);
  and and_8 (and_8_out, Write_enabler, decoder_1_out7);
  and and_9 (and_9_out, Write_enabler, decoder_1_out8);
  and and_10 (and_10_out, Write_enabler, decoder_1_out9);
  and and_11 (and_11_out, Write_enabler, decoder_1_out10);
  and and_12 (and_12_out, Write_enabler, decoder_1_out11);
  and and_13 (and_13_out, Write_enabler, decoder_1_out12);
  and and_14 (and_14_out, Write_enabler, decoder_1_out13);
  and and_15 (and_15_out, Write_enabler, decoder_1_out14);
  and and_16 (and_16_out, Write_enabler, decoder_1_out15);
  Register #(.width(16)) s0 (.D(Bin), .en(and_1_out), .Q(s0_q), .clk(Clock), .clr(Register_clear));
  Register #(.width(16)) s1 (.D(Bin), .en(and_2_out), .Q(s1_q), .clk(Clock), .clr(Register_clear));
  Register #(.width(16)) s2 (.D(Bin), .en(and_3_out), .Q(s2_q), .clk(Clock), .clr(Register_clear));
  Register #(.width(16)) s3 (.D(Bin), .en(and_4_out), .Q(s3_q), .clk(Clock), .clr(Register_clear));
  Register #(.width(16)) s4 (.D(Bin), .en(and_5_out), .Q(s4_q), .clk(Clock), .clr(Register_clear));
  Register #(.width(16)) s5 (.D(Bin), .en(and_6_out), .Q(s5_q), .clk(Clock), .clr(Register_clear));
  Register #(.width(16)) s6 (.D(Bin), .en(and_7_out), .Q(s6_q), .clk(Clock), .clr(Register_clear));
  Register #(.width(16)) s7 (.D(Bin), .en(and_8_out), .Q(s7_q), .clk(Clock), .clr(Register_clear));
  Register #(.width(16)) s8 (.D(Bin), .en(and_9_out), .Q(s8_q), .clk(Clock), .clr(Register_clear));
  Register #(.width(16)) s9 (.D(Bin), .en(and_10_out), .Q(s9_q), .clk(Clock), .clr(Register_clear));
  Register #(.width(16)) s10 (.D(Bin), .en(and_11_out), .Q(s10_q), .clk(Clock), .clr(Register_clear));
  Register #(.width(16)) s11 (.D(Bin), .en(and_12_out), .Q(s11_q), .clk(Clock), .clr(Register_clear));
  Register #(.width(16)) s12 (.D(Bin), .en(and_13_out), .Q(s12_q), .clk(Clock), .clr(Register_clear));
  Register #(.width(16)) s13 (.D(Bin), .en(and_14_out), .Q(s13_q), .clk(Clock), .clr(Register_clear));
  Register #(.width(16)) s14 (.D(Bin), .en(and_15_out), .Q(s14_q), .clk(Clock), .clr(Register_clear));
  Register #(.width(16)) s15 (.D(Bin), .en(and_16_out), .Q(s15_q), .clk(Clock), .clr(Register_clear));
  Multiplexer #(.select(4), .width(16), .enable("false")) multiplexer_1 (
    .in0(s0_q), .in1(s1_q), .in2(s2_q), .in3(s3_q), .in4(s4_q), .in5(s5_q), .in6(s6_q), .in7(s7_q),
    .in8(s8_q), .in9(s9_q), .in10(s10_q), .in11(s11_q), .in12(s12_q), .in13(s13_q), .in14(s14_q),
    .in15(s15_q), .out(Data1_RS), .sel(RS_SELECTOR));
  Multiplexer #(.select(4), .width(16), .enable("false")) multiplexer_2 (
    .in0(s0_q), .in1(s1_q), .in2(s3_q), .in3(s4_q), .in4(s4_q), .in5(s5_q), .in6(s6_q), .in7(s7_q),
    .in8(s8_q), .in9(s9_q), .in10(s10_q), .in11(s11_q), .in12(s12_q), .in13(s13_q), .in14(s14_q),
    .in15(s15_q), .out(Data2_RT), .sel(RT_SELECTOR));
endmodule

module _1bit_ALU_IC (
  input  cin,
  input  A,
  input  Ain,
  input  B,
  input  [1:0] ALU_OPP,
  input  Bin,
  output RES,
  output cout
);

  wire adder_1_out, and_1_out, multiplexer_1_out, multiplexer_2_out, not_1_out, not_2_out, or_1_out;

  not not_1 (not_1_out, A);
  Multiplexer #(.enable("false")) multiplexer_1 (.in0(B), .in1(not_2_out), .out(multiplexer_1_out), .sel(Bin));
  not not_2 (not_2_out, B);
  Multiplexer #(.enable("false")) multiplexer_2 (.in0(A), .in1(not_1_out), .out(multiplexer_2_out), .sel(Ain));
  and and_1 (and_1_out, multiplexer_2_out, multiplexer_1_out);
  or or_1 (or_1_out, multiplexer_2_out, multiplexer_1_out);
  Adder #(.width(1)) adder_1 (.a(multiplexer_2_out), .b(multiplexer_1_out), .out(adder_1_out), .cin(cin), .cout(cout));
  Multiplexer #(.select(2), .enable("false")) multiplexer_3 (
    .in0(and_1_out), .in1(or_1_out), .in2(adder_1_out), .out(RES), .sel(ALU_OPP));  // open: in3
endmodule

module _16_bit_IC (
  input  Cin,
  input  [15:0] A,
  input  [1:0] ALU_OPP,
  input  Ain,
  input  Bin,
  input  [15:0] B,
  output [15:0] RESULT,
  output RD
);

  wire n1bit_alu_ic_1_cout, n1bit_alu_ic_2_cout, n1bit_alu_ic_3_cout, n1bit_alu_ic_4_cout,
       n1bit_alu_ic_5_cout, n1bit_alu_ic_6_cout, n1bit_alu_ic_7_cout, n1bit_alu_ic_8_cout,
       n1bit_alu_ic_9_cout, n1bit_alu_ic_10_cout, n1bit_alu_ic_11_cout, n1bit_alu_ic_12_cout,
       n1bit_alu_ic_13_cout, n1bit_alu_ic_14_cout, n1bit_alu_ic_15_cout, n1bit_alu_ic_16_cout;

  _1bit_ALU_IC u_1bit_alu_ic_1 (
    .A(A[0]), .Ain(Ain), .B(B[0]), .Bin(Bin), .RES(RESULT[0]), .cin(Cin), .ALU_OPP(ALU_OPP),
    .cout(n1bit_alu_ic_1_cout));
  _1bit_ALU_IC u_1bit_alu_ic_2 (
    .A(A[1]), .Ain(Ain), .B(B[1]), .Bin(Bin), .RES(RESULT[1]), .cin(n1bit_alu_ic_1_cout), .ALU_OPP(ALU_OPP),
    .cout(n1bit_alu_ic_2_cout));
  _1bit_ALU_IC u_1bit_alu_ic_3 (
    .A(A[15]), .Ain(Ain), .B(B[15]), .Bin(Bin), .RES(RESULT[15]), .cin(n1bit_alu_ic_2_cout),
    .ALU_OPP(ALU_OPP), .cout(n1bit_alu_ic_3_cout));
  _1bit_ALU_IC u_1bit_alu_ic_4 (
    .A(A[2]), .Ain(Ain), .B(B[2]), .Bin(Bin), .RES(RESULT[2]), .cin(n1bit_alu_ic_3_cout), .ALU_OPP(ALU_OPP),
    .cout(n1bit_alu_ic_4_cout));
  _1bit_ALU_IC u_1bit_alu_ic_5 (
    .A(A[3]), .Ain(Ain), .B(B[3]), .Bin(Bin), .RES(RESULT[3]), .cin(n1bit_alu_ic_4_cout), .ALU_OPP(ALU_OPP),
    .cout(n1bit_alu_ic_5_cout));
  _1bit_ALU_IC u_1bit_alu_ic_6 (
    .A(A[4]), .Ain(Ain), .B(B[4]), .Bin(Bin), .RES(RESULT[4]), .cin(n1bit_alu_ic_5_cout), .ALU_OPP(ALU_OPP),
    .cout(n1bit_alu_ic_6_cout));
  _1bit_ALU_IC u_1bit_alu_ic_7 (
    .A(A[5]), .Ain(Ain), .B(B[5]), .Bin(Bin), .RES(RESULT[5]), .cin(n1bit_alu_ic_6_cout), .ALU_OPP(ALU_OPP),
    .cout(n1bit_alu_ic_7_cout));
  _1bit_ALU_IC u_1bit_alu_ic_8 (
    .A(A[6]), .Ain(Ain), .B(B[6]), .Bin(Bin), .RES(RESULT[6]), .cin(n1bit_alu_ic_7_cout), .ALU_OPP(ALU_OPP),
    .cout(n1bit_alu_ic_8_cout));
  _1bit_ALU_IC u_1bit_alu_ic_9 (
    .A(A[7]), .Ain(Ain), .B(B[7]), .Bin(Bin), .RES(RESULT[7]), .cin(n1bit_alu_ic_8_cout), .ALU_OPP(ALU_OPP),
    .cout(n1bit_alu_ic_9_cout));
  _1bit_ALU_IC u_1bit_alu_ic_10 (
    .A(A[8]), .Ain(Ain), .B(B[8]), .Bin(Bin), .RES(RESULT[8]), .cin(n1bit_alu_ic_9_cout), .ALU_OPP(ALU_OPP),
    .cout(n1bit_alu_ic_10_cout));
  _1bit_ALU_IC u_1bit_alu_ic_11 (
    .A(A[9]), .Ain(Ain), .B(B[9]), .Bin(Bin), .RES(RESULT[9]), .cin(n1bit_alu_ic_10_cout), .ALU_OPP(ALU_OPP),
    .cout(n1bit_alu_ic_11_cout));
  _1bit_ALU_IC u_1bit_alu_ic_12 (
    .A(A[10]), .Ain(Ain), .B(B[10]), .Bin(Bin), .RES(RESULT[10]), .cin(n1bit_alu_ic_11_cout),
    .ALU_OPP(ALU_OPP), .cout(n1bit_alu_ic_12_cout));
  _1bit_ALU_IC u_1bit_alu_ic_13 (
    .A(A[11]), .Ain(Ain), .B(B[11]), .Bin(Bin), .RES(RESULT[11]), .cin(n1bit_alu_ic_12_cout),
    .ALU_OPP(ALU_OPP), .cout(n1bit_alu_ic_13_cout));
  _1bit_ALU_IC u_1bit_alu_ic_14 (
    .A(A[12]), .Ain(Ain), .B(B[12]), .Bin(Bin), .RES(RESULT[12]), .cin(n1bit_alu_ic_13_cout),
    .ALU_OPP(ALU_OPP), .cout(n1bit_alu_ic_14_cout));
  _1bit_ALU_IC u_1bit_alu_ic_15 (
    .A(A[13]), .Ain(Ain), .B(B[13]), .Bin(Bin), .RES(RESULT[13]), .cin(n1bit_alu_ic_14_cout),
    .ALU_OPP(ALU_OPP), .cout(n1bit_alu_ic_15_cout));
  _1bit_ALU_IC u_1bit_alu_ic_16 (
    .A(A[14]), .Ain(Ain), .B(B[14]), .Bin(Bin), .RES(RESULT[14]), .cin(n1bit_alu_ic_15_cout),
    .ALU_OPP(ALU_OPP), .cout(n1bit_alu_ic_16_cout));
  xor xor_1 (RD, n1bit_alu_ic_15_cout, n1bit_alu_ic_16_cout);
endmodule

module _1_bit_alu_2 (
  input  in_1,
  input  in_2,
  input  C_in,
  input  B_Invert,
  input  Less,
  input  [1:0] ALU_Op,
  output ALU_Output,
  output Set,
  output C_out
);

  wire and_1_out, multiplexer_1_out, not_1_out, or_1_out;

  not not_1 (not_1_out, in_1);
  Multiplexer #(.enable("false")) multiplexer_1 (.in0(in_1), .in1(not_1_out), .out(multiplexer_1_out), .sel(B_Invert));
  and and_1 (and_1_out, in_2, in_1);
  or or_1 (or_1_out, in_2, in_1);
  Adder #(.width(1)) adder_1 (.a(in_2), .b(multiplexer_1_out), .out(Set), .cin(C_in), .cout(C_out));
  Multiplexer #(.select(2), .enable("false")) multiplexer_2 (
    .in0(and_1_out), .in1(or_1_out), .in2(Set), .in3(Less), .out(ALU_Output), .sel(ALU_Op));
endmodule

module _16_bit_ALU_2 (
  input  B_Invert,
  input  [15:0] A,
  input  [15:0] B,
  input  [1:0] ALU_Op,
  output Zero_Flag,
  output [15:0] ALU_Output,
  output Overflow_Flag,
  output C_Out
);

  wire undriven;

  xor xor_1 (Overflow_Flag, undriven, C_Out);
  nor nor_1 (Zero_Flag, ALU_Output[0], ALU_Output[1], ALU_Output[2], ALU_Output[3], ALU_Output[4], ALU_Output[5], ALU_Output[6], ALU_Output[7], ALU_Output[8], ALU_Output[9], ALU_Output[10], ALU_Output[11], ALU_Output[12], ALU_Output[13], ALU_Output[14], ALU_Output[15]);

  // Notes on the sheet:
  //   C_In
  //   Set
endmodule

module _16_BIT_IC (
  input  Cin,
  input  [15:0] A,
  input  [1:0] ALU_OPP,
  input  Ain,
  input  Bin,
  input  [15:0] B,
  output [15:0] Res,
  output zero_detector,
  output overflow_detector
);

  wire n1bit_alu_ic_1_cout, n1bit_alu_ic_2_cout, n1bit_alu_ic_3_cout, n1bit_alu_ic_4_cout,
       n1bit_alu_ic_5_cout, n1bit_alu_ic_6_cout, n1bit_alu_ic_7_cout, n1bit_alu_ic_8_cout,
       n1bit_alu_ic_9_cout, n1bit_alu_ic_11_cout, n1bit_alu_ic_12_cout, n1bit_alu_ic_13_cout,
       n1bit_alu_ic_14_cout, n1bit_alu_ic_15_cout, n1bit_alu_ic_16_cout;

  _1bit_ALU_IC u_1bit_alu_ic_1 (
    .A(A[0]), .Ain(Ain), .B(B[0]), .Bin(Bin), .RES(Res[0]), .cin(Cin), .ALU_OPP(ALU_OPP),
    .cout(n1bit_alu_ic_1_cout));
  _1bit_ALU_IC u_1bit_alu_ic_2 (
    .A(A[1]), .Ain(Ain), .B(B[1]), .Bin(Bin), .RES(Res[1]), .cin(n1bit_alu_ic_1_cout), .ALU_OPP(ALU_OPP),
    .cout(n1bit_alu_ic_2_cout));
  _1bit_ALU_IC u_1bit_alu_ic_3 (
    .A(A[2]), .Ain(Ain), .B(B[2]), .Bin(Bin), .RES(Res[2]), .cin(n1bit_alu_ic_2_cout), .ALU_OPP(ALU_OPP),
    .cout(n1bit_alu_ic_3_cout));
  _1bit_ALU_IC u_1bit_alu_ic_4 (
    .A(A[3]), .Ain(Ain), .B(B[3]), .Bin(Bin), .RES(Res[3]), .cin(n1bit_alu_ic_3_cout), .ALU_OPP(ALU_OPP),
    .cout(n1bit_alu_ic_4_cout));
  _1bit_ALU_IC u_1bit_alu_ic_5 (
    .A(A[4]), .Ain(Ain), .B(B[4]), .Bin(Bin), .RES(Res[4]), .cin(n1bit_alu_ic_4_cout), .ALU_OPP(ALU_OPP),
    .cout(n1bit_alu_ic_5_cout));
  _1bit_ALU_IC u_1bit_alu_ic_6 (
    .A(A[5]), .Ain(Ain), .B(B[5]), .Bin(Bin), .RES(Res[5]), .cin(n1bit_alu_ic_5_cout), .ALU_OPP(ALU_OPP),
    .cout(n1bit_alu_ic_6_cout));
  _1bit_ALU_IC u_1bit_alu_ic_7 (
    .A(A[6]), .Ain(Ain), .B(B[6]), .Bin(Bin), .RES(Res[6]), .cin(n1bit_alu_ic_6_cout), .ALU_OPP(ALU_OPP),
    .cout(n1bit_alu_ic_7_cout));
  _1bit_ALU_IC u_1bit_alu_ic_8 (
    .A(A[7]), .Ain(Ain), .B(B[7]), .Bin(Bin), .RES(Res[7]), .cin(n1bit_alu_ic_7_cout), .ALU_OPP(ALU_OPP),
    .cout(n1bit_alu_ic_8_cout));
  _1bit_ALU_IC u_1bit_alu_ic_9 (
    .A(A[8]), .Ain(Ain), .B(B[8]), .Bin(Bin), .RES(Res[8]), .cin(n1bit_alu_ic_8_cout), .ALU_OPP(ALU_OPP),
    .cout(n1bit_alu_ic_9_cout));
  _1bit_ALU_IC u_1bit_alu_ic_10 (
    .A(A[9]), .Ain(Ain), .B(B[9]), .Bin(Bin), .RES(Res[9]), .cin(n1bit_alu_ic_9_cout), .ALU_OPP(ALU_OPP),
    .cout(n1bit_alu_ic_9_cout));
  _1bit_ALU_IC u_1bit_alu_ic_11 (
    .A(A[10]), .Ain(Ain), .B(B[10]), .Bin(Bin), .RES(Res[10]), .cin(n1bit_alu_ic_9_cout), .ALU_OPP(ALU_OPP),
    .cout(n1bit_alu_ic_11_cout));
  _1bit_ALU_IC u_1bit_alu_ic_12 (
    .A(A[11]), .Ain(Ain), .B(B[11]), .Bin(Bin), .RES(Res[11]), .cin(n1bit_alu_ic_11_cout), .ALU_OPP(ALU_OPP),
    .cout(n1bit_alu_ic_12_cout));
  _1bit_ALU_IC u_1bit_alu_ic_13 (
    .A(A[12]), .Ain(Ain), .B(B[12]), .Bin(Bin), .RES(Res[12]), .cin(n1bit_alu_ic_12_cout), .ALU_OPP(ALU_OPP),
    .cout(n1bit_alu_ic_13_cout));
  _1bit_ALU_IC u_1bit_alu_ic_14 (
    .A(A[13]), .Ain(Ain), .B(B[13]), .Bin(Bin), .RES(Res[13]), .cin(n1bit_alu_ic_13_cout), .ALU_OPP(ALU_OPP),
    .cout(n1bit_alu_ic_14_cout));
  _1bit_ALU_IC u_1bit_alu_ic_15 (
    .A(A[14]), .Ain(Ain), .B(B[14]), .Bin(Bin), .RES(Res[14]), .cin(n1bit_alu_ic_14_cout), .ALU_OPP(ALU_OPP),
    .cout(n1bit_alu_ic_15_cout));
  nor nor_1 (zero_detector, Res[0], Res[1], Res[2], Res[3], Res[4], Res[5], Res[6], Res[7], Res[8], Res[9], Res[10], Res[11], Res[12], Res[13], Res[14], Res[15]);
  _1bit_ALU_IC u_1bit_alu_ic_16 (
    .A(A[15]), .Ain(Ain), .B(B[15]), .Bin(Bin), .RES(Res[15]), .cin(n1bit_alu_ic_15_cout), .ALU_OPP(ALU_OPP),
    .cout(n1bit_alu_ic_16_cout));
  xor xor_1 (overflow_detector, n1bit_alu_ic_15_cout, n1bit_alu_ic_16_cout);
endmodule

module R_tpe_data_path_connect (
  input  Cin,
  input  [1:0] ALUopp,
  input  PC_Clear,
  input  Ain,
  input  Bin,
  input  Write_enabler,
  input  Clear_register,
  output [3:0] OP_code,
  output [3:0] RS,
  output [3:0] RT,
  output [3:0] RD,
  output [15:0] Data1_RS,
  output zero,
  output [15:0] Res,
  output overflow,
  output [15:0] Data2_RT
);

  wire Clock_out;
  wire [15:0] adder_1_out, register_1_q;

  Register #(.width(16)) register_1 (.D(adder_1_out), .Q(register_1_q), .clk(Clock_out), .clr(PC_Clear));  // open: en
  Clock Clock (.out(Clock_out));
  Adder #(.width(16)) adder_1 (.a(register_1_q), .b(16'h1), .out(adder_1_out));  // open: cin, cout
  ROM #(.addrWidth(16), .dataWidth(16)) rom_1 (.addr(register_1_q), .data({OP_code, RS, RT, RD}));  // open: sel
  _16_bit_register_file u_16_bit_register_file_1 (
    .Write_enabler(Write_enabler), .RD(RD), .Clock(Clock_out), .Data1_RS(Data1_RS), .RS_SELECTOR(RS),
    .Data2_RT(Data2_RT), .RT_SELECTOR(RT), .Register_clear(Clear_register), .Bin(Res));
  _16_BIT_IC u_16_bit_ic_1 (
    .A(Data1_RS), .ALU_OPP(ALUopp), .Res(Res), .Ain(Ain), .Bin(Bin), .B(Data2_RT), .zero_detector(zero),
    .overflow_detector(overflow), .Cin(Cin));

  // Notes on the sheet:
  //   contents of rom_1 (hex, n*v repeats v):
  //   12
  //   R Type instruction : $s0,$s1,$s3
  //   Foysal
  //   ID-628
endmodule

module ALL_IC (
);

  OR_IC or_ic_1 ();  // open: in_1, in_2, in_3, in_4, in_5, in_6, in_7, in_8, out_9, out_10, out_11, out_12
  NAND_IC nand_ic_1 ();  // open: in_1, in_2, in_3, in_4, in_5, in_6, in_7, in_8, out_9, out_10, out_11, out_12
  NOT_IC not_ic_1 ();  // open: in_1, in_2, in_3, in_4, in_5, in_6, out_7, out_8, out_9, out_10, out_11, out_12
  AND_IC and_ic_1 ();  // open: in_1, in_2, in_3, in_4, in_5, in_6, in_7, in_8, out_9, out_10, out_11, out_12
  NOR_IC nor_ic_1 ();  // open: in_1, in_2, in_3, in_4, in_5, in_6, in_7, in_8, out_9, out_10, out_11, out_12
  _4_1_MUX u_4_1_mux_1 ();  // open: _1, _2, _3, _4, S2, S1, out_7
  D_Flip_flop_IC d_flip_flop_ic_1 ();  // open: Pre_set, Clock, D, Clear, out_5, out_6
  _4_bit_adder_IC u_4_bit_adder_ic_1 ();  // open: A1, B1, CARRY_ON, A2, B2, A3, B3, A4, B4, SUM1, SUM2, SUM3, SUM4, CARRY_OUT
  _1bit_ALU_IC u_1bit_alu_ic_1 ();  // open: A, Ain, B, Bin, RES, cin, ALU_OPP, cout
  _16_BIT_IC u_16_bit_ic_1 ();  // open: A, ALU_OPP, Res, Ain, Bin, B, zero_detector, overflow_detector, Cin
  _16_bit_register_file u_16_bit_register_file_1 ();  // open: Write_enabler, RD, Clock, Data1_RS, RS_SELECTOR, Data2_RT, RT_SELECTOR, Register_clear, Bin

  // Notes on the sheet:
  //   JOBAER AHMED
  //   ID- 411220300426 
endmodule
